# Fritzing sketch NovoPainel (saved by Fritzing 0.9.2b)
circuit board: 19cm x 5.64444cm
breadboards: 1

parts:
  J1 = female pin header, 2 pins [form="♀ (female)"]
  J2 = female pin header, 2 pins [form="♀ (female)"]
  S1 = SWITCH-MOMENTARY-2 [package=tactile-switch-1101ne]
  J3 = female pin header, 2 pins [form="♀ (female)"]
  C1 = Electrolytic Capacitor [capacitance=100µF package="200 mil [THT, electrolytic]"]
  S2 = SWITCH-MOMENTARY-2 [package=tactile-switch-1101ne]

nets:
  N1: J1.pin1, J2.pin1, S1.1
  N2: J1.pin2, J2.pin2, J3.pin2, C1.-
  N3: S1.2, J3.pin1, C1.+, S2.1

notes:
  +
  -
  B1
  B2
  V1
  S1
  Baterias em paralelo
  Verificar tamanho do borne para ajustar na pcb
